# Fritzing sketch esa-02-ske (saved by Fritzing 0.9.4)
breadboards: 1

parts:
  Part1 = Arduino Uno (Rev3)
  LED1 = smd LED [color="Red (633nm)" package="1206 [SMD]"]
  R2 = Resistor [tolerance=±5% resistance=4.7k package="1206 [SMD]"]
  R1 = Temperature Sensor (Thermistor) [thermistor_type=NTC package=THT]

nets:
  N1: Part1.A0, R2.Pin_0, R1.pin_1
  N2: Part1.D13/SCK, LED1.anode
  N3: Part1.AREF, Part1.5V, R1.pin_0
  N4: Part1.GND, LED1.cathode, R2.Pin_1
