# Fritzing sketch esa-03-ske2 (saved by Fritzing 0.9.4)
breadboards: 1

parts:
  Part1 = Arduino Uno (Rev3)
  S1 = Momentary Switch [package=ksa_sealed_tac_switch]
  R1 = Resistor [tolerance=±5% resistance=220 package=THT]

nets:
  N1: Part1.D2, S1.3
  N2: Part1.5V, R1.Pin_0
  N3: Part1.GND, S1.2
  N4: S1.4, R1.Pin_1
