# Fritzing sketch esa-04 (saved by Fritzing 0.9.4)
breadboards: 1

parts:
  R1 = Resistor [tolerance=±5% resistance=470 package="0603 [SMD]"]
  R2 = Resistor [tolerance=±5% resistance=4.7k package="0603 [SMD]"]
  R3 = Resistor [tolerance=±5% resistance=47k package="0603 [SMD]"]
  R4 = Resistor [tolerance=±5% resistance=47 package="0603 [SMD]"]
  R5 = Resistor [tolerance=±5% resistance=220 package="0603 [SMD]"]
  Part1 = Arduino Uno (Rev3) - ICSP

nets:
  N1: R1.Pin_0, Part1.D4
  N2: R1.Pin_1, R2.Pin_1, R3.Pin_1, R4.Pin_1, R5.Pin_0, Part1.A0
  N3: R2.Pin_0, Part1.D3_PWM
  N4: R3.Pin_0, Part1.D2
  N5: R4.Pin_0, Part1.D5_PWM
  N6: R5.Pin_1, Part1.GND
