# Fritzing sketch esa-05-ske (saved by Fritzing 0.9.4)
breadboards: 1

parts:
  R5 = Resistor [tolerance=±5% resistance=220 package="0603 [SMD]"]
  Part1 = Arduino Uno (Rev3) - ICSP
  R6 = Resistor [tolerance=±5% resistance=100 package="0603 [SMD]"]
  LED1 = smd LED [color="Red (633nm)" package="1206 [SMD]"]
  C1 = Electrolytic Capacitor [capacitance=1μF package="0405 [SMD, electrolytic]"]
  R7 = Resistor [tolerance=±5% resistance=10k package=THT]
  S1 = Pushbutton [package="[THT]"]

nets:
  N1: R5.Pin_0, Part1.D5_PWM
  N2: R5.Pin_1, Part1.A1, R6.Pin_0, C1.+
  N3: Part1.A0, R6.Pin_1, LED1.anode
  N4: Part1.D2, R7.Pin_0, S1.Pin_1, S1.Pin_2
  N5: Part1.5V, S1.Pin_3, S1.Pin_4
  N6: Part1.GND, LED1.cathode, C1.-, R7.Pin_1
